// Logisim project proyectoFinal.circ as structural Verilog: 1 circuit, main circuit main
module main (
  input  in_1,
  input  in_2,
  input  in_3,
  input  in_4,
  input  in_5,
  input  in_6,
  input  in_7,
  input  in_8,
  input  in_9,
  input  in_10,
  input  in_11,
  input  in_12,
  input  in_13,
  input  in_14,
  input  in_15,
  input  in_16
);

  wire _30f1, _30f2, _30f3, _30f4, _30f5, _30f6, _30f7, _30f8, _30f9, _30f10, _30f11, _30f12, _30f13, _30f14,
       _31f1, _31f2, _31f3, _31f4, _31f5, _31f6, _31f7, _31f8, _31f9, _31f10, _31f11, _31f12, _31f13, _31f14,
       button_2_out, d1a, d2a, d2b, d3a, d3b, d4a, d4b, d5a, d5b, d6a, d6b, d7a, d7b, d8a, d8b, d22a,
       d_ff_33_q, dir, e, e1, e2, e3, e4, e5, e6, e7, e8, e9, e10, e11, e12, e13, e14, e15, e16, e17, e18,
       e19, e20, e21, e22, e23, e24, e25, e26, e27, e28, e29, e30, e31, e32, neg, not_3_out, not_4_out,
       not_5_out, not_6_out, not_7_out, not_8_out, not_9_out, or_29_out, or_30_out, or_31_out, or_32_out,
       or_33_out, or_34_out, or_35_out, pr, prn, rj, s1, s2, s3, s4, s5, s6, s7, so1, so2, so3, so4, so5,
       so6, so7, sp1, sp2, sp3, sp4, sp5, sp6, sp7;

  Clock clock_1 (.out(rj));
  not not_1 (neg, in_1);
  not not_2 (prn, pr);
  Multiplexer #(.enable("false")) multiplexer_1 (.in0(in_3), .in1(neg), .out(sp1), .sel(not_3_out));
  not not_3 (not_3_out, s1);
  Multiplexer #(.enable("false")) multiplexer_2 (.in0(in_11), .in1(neg), .out(sp5), .sel(not_4_out));
  not not_4 (not_4_out, s5);
  D_Flip_Flop d_ff_1 (.clk(rj), .D(e32), .Q(e1), .preset(pr));  // open: Qn, en, reset
  D_Flip_Flop d_ff_2 (.clk(rj), .D(e8), .Q(e9));  // open: Qn, preset, en, reset
  D_Flip_Flop d_ff_3 (.clk(rj), .D(e16), .Q(e17));  // open: Qn, preset, en, reset
  D_Flip_Flop d_ff_4 (.clk(rj), .D(e24), .Q(e25));  // open: Qn, preset, en, reset
  Multiplexer #(.enable("false")) multiplexer_3 (.in0(in_5), .in1(neg), .out(so1), .sel(s1));
  Multiplexer #(.enable("false")) multiplexer_4 (.in0(in_13), .in1(neg), .out(so5), .sel(s5));
  or or_1 (_31f1, sp1, e31);
  or or_2 (_31f2, sp2, e31);
  or or_3 (_30f1, sp1, e30);
  or or_4 (_30f2, sp2, e30);
  D_Flip_Flop d_ff_5 (.clk(rj), .D(e1), .Q(e2), .preset(pr));  // open: Qn, en, reset
  D_Flip_Flop d_ff_6 (.clk(rj), .D(e9), .Q(e10));  // open: Qn, preset, en, reset
  D_Flip_Flop d_ff_7 (.clk(rj), .D(e17), .Q(e18));  // open: Qn, preset, en, reset
  D_Flip_Flop d_ff_8 (.clk(rj), .D(e25), .Q(e26));  // open: Qn, preset, en, reset
  Multiplexer #(.enable("false")) multiplexer_5 (.in0(in_4), .in1(neg), .out(sp2), .sel(not_5_out));
  not not_5 (not_5_out, s2);
  Multiplexer #(.enable("false")) multiplexer_6 (.in0(in_12), .in1(neg), .out(sp6), .sel(not_6_out));
  not not_6 (not_6_out, s6);
  or or_5 (_31f3, sp3, e31);
  or or_6 (_31f4, sp4, e31);
  or or_7 (_31f5, sp5, e31);
  or or_8 (_30f3, sp3, e30);
  or or_9 (_30f4, sp4, e30);
  or or_10 (_30f5, sp5, e30);
  D_Flip_Flop d_ff_9 (.clk(rj), .D(e2), .Q(e3), .en(prn));  // open: Qn, preset, reset
  D_Flip_Flop d_ff_10 (.clk(rj), .D(e10), .Q(e11));  // open: Qn, preset, en, reset
  D_Flip_Flop d_ff_11 (.clk(rj), .D(e18), .Q(e19));  // open: Qn, preset, en, reset
  D_Flip_Flop d_ff_12 (.clk(rj), .D(e26), .Q(e27));  // open: Qn, preset, en, reset
  Multiplexer #(.enable("false")) multiplexer_7 (.in0(in_6), .in1(neg), .out(so2), .sel(s2));
  Multiplexer #(.enable("false")) multiplexer_8 (.in0(in_14), .in1(neg), .out(so6), .sel(s6));
  or or_11 (_31f6, sp6, e31);
  or or_12 (_31f7, sp7, e31);
  or or_13 (_31f8, so1, e31);
  or or_14 (_30f6, sp6, e30);
  or or_15 (_30f7, sp7, e30);
  or or_16 (_30f8, so1, e30);
  D_Flip_Flop d_ff_13 (.clk(rj), .D(e3), .Q(e4));  // open: Qn, preset, en, reset
  D_Flip_Flop d_ff_14 (.clk(rj), .D(e11), .Q(e12));  // open: Qn, preset, en, reset
  D_Flip_Flop d_ff_15 (.clk(rj), .D(e19), .Q(e20));  // open: Qn, preset, en, reset
  D_Flip_Flop d_ff_16 (.clk(rj), .D(e27), .Q(e28));  // open: Qn, preset, en, reset
  Multiplexer #(.enable("false")) multiplexer_9 (.in0(in_7), .in1(neg), .out(sp3), .sel(not_7_out));
  not not_7 (not_7_out, s3);
  Multiplexer #(.enable("false")) multiplexer_10 (.in0(in_15), .in1(neg), .out(sp7), .sel(not_8_out));
  not not_8 (not_8_out, s7);
  or or_17 (_31f9, so2, e31);
  or or_18 (_31f10, so3, e31);
  or or_19 (_31f11, so4, e31);
  or or_20 (_30f9, so2, e30);
  or or_21 (_30f10, so3, e30);
  or or_22 (_30f11, so4, e30);
  D_Flip_Flop d_ff_17 (.clk(rj), .D(e4), .Q(e5));  // open: Qn, preset, en, reset
  D_Flip_Flop d_ff_18 (.clk(rj), .D(e12), .Q(e13));  // open: Qn, preset, en, reset
  D_Flip_Flop d_ff_19 (.clk(rj), .D(e20), .Q(e21));  // open: Qn, preset, en, reset
  D_Flip_Flop d_ff_20 (.clk(rj), .D(e28), .Q(e29));  // open: Qn, preset, en, reset
  Multiplexer #(.enable("false")) multiplexer_11 (.in0(in_9), .in1(neg), .out(so3), .sel(s3));
  Multiplexer #(.enable("false")) multiplexer_12 (.in0(in_16), .in1(neg), .out(so7), .sel(s7));
  or or_23 (_31f12, so5, e31);
  or or_24 (_31f13, so6, e31);
  or or_25 (_31f14, so7, e31);
  or or_26 (_30f12, so5, e30);
  or or_27 (_30f13, so6, e30);
  or or_28 (_30f14, so7, e30);
  D_Flip_Flop d_ff_21 (.clk(rj), .D(e5), .Q(e6));  // open: Qn, preset, en, reset
  D_Flip_Flop d_ff_22 (.clk(rj), .D(e13), .Q(e14));  // open: Qn, preset, en, reset
  D_Flip_Flop d_ff_23 (.clk(rj), .D(e21), .Q(e22));  // open: Qn, preset, en, reset
  D_Flip_Flop d_ff_24 (.clk(rj), .D(e29), .Q(e30));  // open: Qn, preset, en, reset
  Multiplexer #(.enable("false")) multiplexer_13 (.in0(in_8), .in1(neg), .out(sp4), .sel(not_9_out));
  not not_9 (not_9_out, s4);
  D_Flip_Flop d_ff_25 (.clk(rj), .D(e6), .Q(e7));  // open: Qn, preset, en, reset
  D_Flip_Flop d_ff_26 (.clk(rj), .D(e14), .Q(e15));  // open: Qn, preset, en, reset
  D_Flip_Flop d_ff_27 (.clk(rj), .D(e22), .Q(e23));  // open: Qn, preset, en, reset
  D_Flip_Flop d_ff_28 (.clk(rj), .D(e30), .Q(e31));  // open: Qn, preset, en, reset
  Multiplexer #(.enable("false")) multiplexer_14 (.in0(in_10), .in1(neg), .out(so4), .sel(s4));
  D_Flip_Flop d_ff_29 (.clk(rj), .D(e7), .Q(e8));  // open: Qn, preset, en, reset
  D_Flip_Flop d_ff_30 (.clk(rj), .D(e15), .Q(e16));  // open: Qn, preset, en, reset
  D_Flip_Flop d_ff_31 (.clk(rj), .D(e23), .Q(e24));  // open: Qn, preset, en, reset
  D_Flip_Flop d_ff_32 (.clk(rj), .D(e31), .Q(e32));  // open: Qn, preset, en, reset
  Button button_1 (.out(pr));
  DotMatrix #(.inputtype("row"), .matrixcols(32), .matrixrows(16)) dotmatrix_1 (
    .row0({e32, e31, e30, e29, e28, e27, e26, e25, e24, e23, e22, e21, e20, e19, e18, e17, e16, e15, e14, e13, e12, e11, e10, e9, e8, e7, e6, e5, e4, e3, e2, e1}),
    .row1({e32, e31, e30, e29, e28, e27, e26, e25, e24, e23, e22, e21, e20, e19, e18, e17, e16, e15, e14, e13, e12, e11, e10, e9, e8, e7, e6, e5, e4, e3, e2, e1}),
    .row2({e32, _31f14, _30f14, e29, e28, e27, e26, e25, e24, e23, e22, e21, e20, e19, e18, e17, e16, e15, e14, e13, e12, e11, e10, e9, e8, e7, e6, e5, e4, e3, e2, e1}),
    .row3({e32, _31f13, _30f13, e29, e28, e27, e26, e25, e24, e23, e22, e21, e20, e19, e18, e17, e16, e15, e14, e13, e12, e11, e10, e9, e8, e7, e6, e5, e4, e3, e2, e1}),
    .row4({e32, _31f12, _30f12, e29, e28, e27, e26, e25, e24, e23, e22, e21, e20, e19, e18, e17, e16, e15, e14, e13, e12, e11, e10, e9, e8, e7, e6, e5, e4, e3, e2, e1}),
    .row5({e32, _31f11, _30f11, e29, e28, e27, e26, e25, e24, e23, e22, e21, e20, e19, e18, e17, e16, e15, e14, e13, e12, e11, e10, e9, e8, e7, e6, e5, e4, e3, e2, e1}),
    .row6({e32, _31f10, _30f10, e29, e28, e27, e26, e25, e24, e23, e22, e21, e20, e19, e18, e17, e16, e15, e14, e13, e12, e11, e10, e9, e8, e7, e6, e5, e4, e3, e2, e1}),
    .row7({e32, _31f9, _30f9, e29, e28, e27, e26, e25, e24, e23, e22, e21, e20, e19, e18, e17, e16, e15, e14, e13, e12, e11, e10, e9, e8, e7, e6, e5, e4, e3, e2, e1}),
    .row8({e32, _31f8, _30f8, e29, e28, e27, e26, e25, e24, e23, e22, e21, e20, e19, e18, e17, e16, e15, e14, e13, e12, e11, e10, e9, e8, e7, e6, e5, e4, e3, e2, e1}),
    .row9({e32, _31f7, _30f7, e29, e28, e27, e26, e25, e24, e23, e22, e21, e20, e19, e18, e17, e16, e15, e14, e13, e12, e11, e10, e9, e8, e7, e6, e5, e4, e3, e2, e1}),
    .row10({e32, _31f6, _30f6, e29, e28, e27, e26, e25, e24, e23, e22, e21, e20, e19, e18, e17, e16, e15, e14, e13, e12, e11, e10, e9, e8, e7, e6, e5, e4, e3, e2, e1}),
    .row11({e32, _31f5, _30f5, e29, e28, e27, e26, e25, e24, e23, e22, e21, e20, e19, e18, e17, e16, e15, e14, e13, e12, e11, e10, e9, e8, e7, e6, e5, e4, e3, e2, e1}),
    .row12({e32, _31f4, _30f4, e29, e28, e27, e26, e25, e24, e23, e22, e21, e20, e19, e18, e17, e16, e15, e14, e13, e12, e11, e10, e9, e8, e7, e6, e5, e4, e3, e2, e1}),
    .row13({e32, _31f3, _30f3, e29, e28, e27, e26, e25, e24, e23, e22, e21, e20, e19, e18, e17, e16, e15, e14, e13, e12, e11, e10, e9, e8, e7, e6, e5, e4, e3, e2, e1}),
    .row14({e32, _31f2, _30f2, e29, e28, e27, e26, e25, e24, e23, e22, e21, e20, e19, e18, e17, e16, e15, e14, e13, e12, e11, e10, e9, e8, e7, e6, e5, e4, e3, e2, e1}),
    .row15({e32, _31f1, _30f1, e29, e28, e27, e26, e25, e24, e23, e22, e21, e20, e19, e18, e17, e16, e15, e14, e13, e12, e11, e10, e9, e8, e7, e6, e5, e4, e3, e2, e1}));
  D_Flip_Flop d_ff_33 (.clk(rj), .Q(d_ff_33_q), .preset(button_2_out), .reset(e));  // open: D, Qn, en
  Button button_2 (.out(button_2_out));
  or or_29 (or_29_out, d1a, d3b);
  or or_30 (or_30_out, d2a, d4b);
  or or_31 (or_31_out, d3a, d5b);
  or or_32 (or_32_out, d4a, d6b);
  or or_33 (or_33_out, d5a, d7b);
  or or_34 (or_34_out, d6a, d8b);
  or or_35 (or_35_out, d7a, in_2);
  Demultiplexer #(.disabled(0), .enable("false")) demultiplexer_1 (.out0(d1a), .out1(d22a), .in(d_ff_33_q), .sel(dir));
  D_Flip_Flop d_ff_34 (.clk(rj), .D(or_29_out), .Q(s1));  // open: Qn, preset, en, reset
  D_Flip_Flop d_ff_35 (.clk(rj), .D(or_30_out), .Q(s2));  // open: Qn, preset, en, reset
  D_Flip_Flop d_ff_36 (.clk(rj), .D(or_31_out), .Q(s3));  // open: Qn, preset, en, reset
  D_Flip_Flop d_ff_37 (.clk(rj), .D(or_32_out), .Q(s4));  // open: Qn, preset, en, reset
  D_Flip_Flop d_ff_38 (.clk(rj), .D(or_33_out), .Q(s5));  // open: Qn, preset, en, reset
  D_Flip_Flop d_ff_39 (.clk(rj), .D(or_34_out), .Q(s6));  // open: Qn, preset, en, reset
  D_Flip_Flop d_ff_40 (.clk(rj), .D(or_35_out), .Q(s7));  // open: Qn, preset, en, reset
  Demultiplexer #(.disabled(0), .enable("false")) demultiplexer_2 (.out0(d2a), .out1(d2b), .in(s1), .sel(dir));
  Demultiplexer #(.disabled(0), .enable("false")) demultiplexer_3 (.out0(d3a), .out1(d3b), .in(s2), .sel(dir));
  Demultiplexer #(.disabled(0), .enable("false")) demultiplexer_4 (.out0(d4a), .out1(d4b), .in(s3), .sel(dir));
  Demultiplexer #(.disabled(0), .enable("false")) demultiplexer_5 (.out0(d5a), .out1(d5b), .in(s4), .sel(dir));
  Demultiplexer #(.disabled(0), .enable("false")) demultiplexer_6 (.out0(d6a), .out1(d6b), .in(s5), .sel(dir));
  Demultiplexer #(.disabled(0), .enable("false")) demultiplexer_7 (.out0(d7a), .out1(d7b), .in(s6), .sel(dir));
  Demultiplexer #(.disabled(0), .enable("false")) demultiplexer_8 (.out0(d8a), .out1(d8b), .in(s7), .sel(dir));
  Comparator #(.width(1)) comparator_1 (.a(d2b), .b(s1), .lt(e));  // open: gt, eq
  T_Flip_Flop t_ff_1 (.Q(dir), .preset(s7), .reset(e));  // open: clk, T, Qn, en

  // Other names for the same wires on the sheet: t1[31:0] = {e32, _31f1, _30f1, e29, e28, e27, e26, e25, e24, e23, e22, e21, e20, e19, e18, e17, e16, e15, e14, e13, e12, e11, e10, e9, e8, e7, e6, e5, e4, e3, e2, e1};
  //   t2[31:0] = {e32, _31f2, _30f2, e29, e28, e27, e26, e25, e24, e23, e22, e21, e20, e19, e18, e17, e16, e15, e14, e13, e12, e11, e10, e9, e8, e7, e6, e5, e4, e3, e2, e1};
  //   t3[31:0] = {e32, _31f3, _30f3, e29, e28, e27, e26, e25, e24, e23, e22, e21, e20, e19, e18, e17, e16, e15, e14, e13, e12, e11, e10, e9, e8, e7, e6, e5, e4, e3, e2, e1};
  //   t4[31:0] = {e32, _31f4, _30f4, e29, e28, e27, e26, e25, e24, e23, e22, e21, e20, e19, e18, e17, e16, e15, e14, e13, e12, e11, e10, e9, e8, e7, e6, e5, e4, e3, e2, e1};
  //   t5[31:0] = {e32, _31f5, _30f5, e29, e28, e27, e26, e25, e24, e23, e22, e21, e20, e19, e18, e17, e16, e15, e14, e13, e12, e11, e10, e9, e8, e7, e6, e5, e4, e3, e2, e1};
  //   t6[31:0] = {e32, _31f6, _30f6, e29, e28, e27, e26, e25, e24, e23, e22, e21, e20, e19, e18, e17, e16, e15, e14, e13, e12, e11, e10, e9, e8, e7, e6, e5, e4, e3, e2, e1};
  //   t7[31:0] = {e32, _31f7, _30f7, e29, e28, e27, e26, e25, e24, e23, e22, e21, e20, e19, e18, e17, e16, e15, e14, e13, e12, e11, e10, e9, e8, e7, e6, e5, e4, e3, e2, e1};
  //   t8[31:0] = {e32, _31f8, _30f8, e29, e28, e27, e26, e25, e24, e23, e22, e21, e20, e19, e18, e17, e16, e15, e14, e13, e12, e11, e10, e9, e8, e7, e6, e5, e4, e3, e2, e1};
  //   t9[31:0] = {e32, _31f9, _30f9, e29, e28, e27, e26, e25, e24, e23, e22, e21, e20, e19, e18, e17, e16, e15, e14, e13, e12, e11, e10, e9, e8, e7, e6, e5, e4, e3, e2, e1};
  //   t10[31:0] = {e32, _31f10, _30f10, e29, e28, e27, e26, e25, e24, e23, e22, e21, e20, e19, e18, e17, e16, e15, e14, e13, e12, e11, e10, e9, e8, e7, e6, e5, e4, e3, e2, e1};
  //   t11[31:0] = {e32, _31f11, _30f11, e29, e28, e27, e26, e25, e24, e23, e22, e21, e20, e19, e18, e17, e16, e15, e14, e13, e12, e11, e10, e9, e8, e7, e6, e5, e4, e3, e2, e1};
  //   t12[31:0] = {e32, _31f12, _30f12, e29, e28, e27, e26, e25, e24, e23, e22, e21, e20, e19, e18, e17, e16, e15, e14, e13, e12, e11, e10, e9, e8, e7, e6, e5, e4, e3, e2, e1};
  //   t13[31:0] = {e32, _31f13, _30f13, e29, e28, e27, e26, e25, e24, e23, e22, e21, e20, e19, e18, e17, e16, e15, e14, e13, e12, e11, e10, e9, e8, e7, e6, e5, e4, e3, e2, e1};
  //   t14[31:0] = {e32, _31f14, _30f14, e29, e28, e27, e26, e25, e24, e23, e22, e21, e20, e19, e18, e17, e16, e15, e14, e13, e12, e11, e10, e9, e8, e7, e6, e5, e4, e3, e2, e1};
  //   t15[31:0] = {e32, e31, e30, e29, e28, e27, e26, e25, e24, e23, e22, e21, e20, e19, e18, e17, e16, e15, e14, e13, e12, e11, e10, e9, e8, e7, e6, e5, e4, e3, e2, e1};
  //   t16[31:0] = {e32, e31, e30, e29, e28, e27, e26, e25, e24, e23, e22, e21, e20, e19, e18, e17, e16, e15, e14, e13, e12, e11, e10, e9, e8, e7, e6, e5, e4, e3, e2, e1}

  // Notes on the sheet:
  //   muñeco: 2x8
  //   obstaculo abajo: 2x5
  //   obstaculo arriba: 2x10
  //   Jugar
endmodule
