// Logisim project proyectoObstaculo.circ as structural Verilog: 1 circuit, main circuit main
module main (
  input  in_1,
  input  in_2,
  input  in_3,
  input  in_4,
  input  in_5,
  input  in_6,
  input  in_7,
  input  in_8,
  input  in_9,
  input  in_10
);

  wire button_1_out, e1, e2, e3, e4, jp, not_5_out, rj;
  wire [0:0] t2, t3, t4;
  wire [2:0] t1;

  Clock clock_1 (.out(rj));
  not not_1 (t1[0], in_3);
  not not_2 (t1[2], in_7);
  D_Flip_Flop d_ff_1 (.clk(rj), .D(e4), .Q(e1));  // open: Qn, preset, en, reset
  D_Flip_Flop d_ff_2 (.clk(rj), .D(e3), .Q(e4));  // open: Qn, preset, en, reset
  not not_3 (t2[0], in_4);
  D_Flip_Flop d_ff_3 (.clk(rj), .D(e1), .Q(e2));  // open: Qn, preset, en, reset
  DotMatrix #(.matrixcols(4), .matrixrows(3)) dotmatrix_1 (
    .col0({t1[2], jp, t1[0]}), .col1({in_10, e4, t4[0]}), .col2({in_9, e3, t3[0]}), .col3({in_8, e2, t2[0]}));
  D_Flip_Flop d_ff_4 (.clk(rj), .D(e2), .Q(e3));  // open: Qn, preset, en, reset
  not not_4 (t3[0], in_5);
  not not_5 (not_5_out, in_1);
  Button button_1 (.out(button_1_out));
  not not_6 (t4[0], in_6);
  Multiplexer #(.enable("false")) multiplexer_1 (.in0(not_5_out), .in1(in_2), .out(jp), .sel(button_1_out));

  // Other names for the same wires on the sheet: t1[1] = jp; t2[2:1] = {in_8, e2}; t3[2:1] = {in_9, e3};
  //   t4[2:1] = {in_10, e4}

  // Notes on the sheet:
  //   if e1 and 2 : restart
endmodule
